# Fritzing sketch educational_Pelican_PCB (saved by Fritzing 0.6.3b)
breadboards: 1

parts:
  S1 = Pushbutton [package="[THT]"]
  A = LED - 5mm [color="Orange (620nm)" package="5 mm [THT]"]
  G = LED - 5mm [color="Green (565nm)" package="5 mm [THT]"]
  RM = LED - 5mm [color="Red (633nm)" package="5 mm [THT]"]
  GM = LED - 5mm [color="Green (565nm)" package="5 mm [THT]"]
  IC1 = IC, DIP package, 8 pins [chip_label=IC spacing=300mil]
  R = LED - 5mm [color="Red (633nm)" package="5 mm [THT]"]
  VCC1 = Cell Coin Holder [part_number="Keystone 500"]

nets:
  N1: S1.Pin_1, S1.Pin_2, IC1.pin1
  N2: S1.Pin_3, S1.Pin_4, A.cathode, G.cathode, RM.cathode, GM.cathode, IC1.pin4, R.cathode, VCC1.-
  N3: A.anode, IC1.pin6
  N4: G.anode, IC1.pin5
  N5: RM.anode, IC1.pin3
  N6: GM.anode, IC1.pin2
  N7: IC1.pin7, R.anode
  N8: IC1.pin8, VCC1.+

custom parts:
  Cell Coin Holder: Body Material PBT For Battery Size Coin Cell Maximum Cell Diameter 12mm Mount PCB Number of Cells 1 (Coin Cell) Terminal Contact Material Spring Steel Terminal Contact Type Top Spring Arm Type Battery Holder
